# Fritzing sketch PiGpioOccupationPlanned (saved by Fritzing 0.9.3b)

parts:
  M1 = DC Motor
  Raspberry_Pi_1 = Raspberry Pi 3 [part_number=RPI-3-V1.2]
  S1 = H-Bridge with L298N
  U1 = LIPO-2000mAh [package=lipo-2000]
  U2 = LIPO-2000mAh [package=lipo-2000]
  M2 = DC Motor
  Reg1 = DC-DC CONVERTER [part_number=80633 package=dc-dc_converter]
  JP1 = USB_MICROB_PLUG [package=micro-b-th]
  Reg2 = DC-DC CONVERTER [part_number=80633 package=dc-dc_converter]
  J1 = Basic Servo

nets:
  N1: M1.pin_1, S1.M1-02
  N2: M1.pin_2, S1.M1-01
  N3: Raspberry_Pi_1.GPIO17, S1.ENB
  N4: Raspberry_Pi_1.GPIO27, S1.IN3
  N5: Raspberry_Pi_1.GPIO22, S1.IN4
  N6: Raspberry_Pi_1.GPIO21, S1.IN1
  N7: Raspberry_Pi_1.GPIO20, S1.IN2
  N8: Raspberry_Pi_1.GPIO16, S1.ENA
  N9: Raspberry_Pi_1.GPIO18, J1.pulse
  GND: Raspberry_Pi_1.GND, J1.gnd
  5V: Raspberry_Pi_1.5V, J1.vcc
  N10: S1.12V, Reg1.OUT-
  N11: S1.GND, Reg1.OUT+
  N12: S1.M2-01, M2.pin_1
  N13: S1.M2-02, M2.pin_2
  N14: U1.+, Reg1.IN-, Reg2.IN-
  N15: U1.-, U2.+
  N16: U2.-, Reg1.IN+, Reg2.IN+
  N17: JP1.VCC, Reg2.OUT-
  N18: JP1.GND, Reg2.OUT+

custom parts:
  H-Bridge with L298N: h-bridge
  DC-DC CONVERTER: WYHP 5A constant current/voltage manufactured by Shenzhen Weiyapuhua Technology Co., Ltd
